# Fritzing sketch esp32 gc blinker (saved by Fritzing 0.9.3b)
breadboards: 1

parts:
  R1 = Resistor [tolerance=±5% resistance=1k package="0805 [SMD]"]
  A2 = Esp32-c3 super mini
  R2 = PHOTOCELL [package=photocell]
  R3 = Resistor [tolerance=±5% resistance=220 package="2512 [SMD]"]
  LED1 = RGB LED (com. anode, rbg) [package="5 mm [THT]"]
  R4 = Resistor [tolerance=±5% resistance=220 package="2512 [SMD]"]
  R5 = Resistor [tolerance=±5% resistance=220 package="2512 [SMD]"]

nets:
  N1: R1.Pin_0, A2.Pin_9, R2.P$2
  N2: R1.Pin_1, A2.Pin_15
  N3: A2.Pin_1, R4.Pin_1
  N4: A2.Pin_2, R5.Pin_1
  N5: A2.Pin_3, R3.Pin_1
  N6: A2.Pin_14, R2.P$1, LED1.common_anode
  N7: R3.Pin_0, LED1.green_cathode
  N8: LED1.red_cathode, R4.Pin_0
  N9: LED1.blue_cathode, R5.Pin_0

custom parts:
  Esp32-c3 super mini: ESP32-C3 Development Board ESP32 SuperMini Development Board ESP32 Development Board WiFi Bluetooth.
